# Fritzing sketch meteo (saved by Fritzing 0.9.2b)
circuit board: 12.9897cm x 1.91301cm

parts:
  Arduino_Pro_Mini_Atmega328 = Arduino Pro Mini Atmega328
  Pad1 = Pad [width=8.15921693659805 height=1.78833629826251 connect=center]
  Pad2 = Pad [width=8.15921693659805 height=1.78833629826251 connect=center]  # not connected
  Pad3 = Pad [width=8.15921693659805 height=1.78833629826251 connect=center]
  Pad4 = Pad [width=8.15921693659805 height=1.78833629826251 connect=center]
  S1 = Tilt Switch [package=THT]
  7_Segment_4_Digit_Display1 = 7-segment-4-digit-common-cathode-display [part_number=CA56-12SRWA package=7-segment-4digit-cathode]  # not connected
  U1 = A23 battery [part_number=MN21 package=battery-a23]
  D1 = Schottky Diode [part_number=1N5817 package="300 mil [THT]"]

nets:
  N1: Arduino_Pro_Mini_Atmega328.A6, S1.Pin_1
  N2: Arduino_Pro_Mini_Atmega328.A7, Pad3.pad
  N3: Arduino_Pro_Mini_Atmega328.GND#24, U1.-1, U1.-2
  N4: Arduino_Pro_Mini_Atmega328.RAW, D1.cathode
  N5: Arduino_Pro_Mini_Atmega328.VCC, Pad1.pad
  N6: Arduino_Pro_Mini_Atmega328.GND#45, Pad4.pad, S1.Pin_2
  N7: U1.+1, U1.+2, D1.anode

custom parts:
  Arduino Pro Mini Atmega328: Arduino Pro Mini based on Atmega328. This is a 5V Arduino running the 16MHz bootloader. There is a voltage regulator on board so it can accept voltage up to 12VDC. If you're supplying unregulated power to the board, be sure to connect to the "RAW" pin on not VCC.
  7-segment-4-digit-common-cathode-display: A 7 Segment 4 Digit common cathode display, with decimal points
  A23 battery: A23 battery (Duracell MN21 and Keystone holders No82)
